# Fritzing sketch MainBoard (saved by Fritzing 0.9.3b)
circuit board: 18cm x 7.5cm

parts:
  CT8z = female pin header, 3 pins [form="♀ (female)"]
  R1 = Resistor [tolerance=±5% resistance=10k package=THT]
  R2 = Resistor [tolerance=±5% resistance=10k package=THT]
  R3 = Resistor [tolerance=±5% resistance=10k package=THT]
  C1 = Ceramic Capacitor [capacitance=22pF package="100 mil [THT, multilayer]"]
  C2 = Ceramic Capacitor [capacitance=22pF package="100 mil [THT, multilayer]"]
  R4 = Resistor [tolerance=±5% resistance=10k package=THT]
  C3 = Ceramic Capacitor [capacitance=100nF package="100 mil [THT, multilayer]"]
  RESET = Pushbutton [package="[THT]"]
  R5 = Resistor [tolerance=±5% resistance=10k package=THT]
  U3 = V_REG_LD1117VXX [package=78xxl]
  U4 = Voltage Regulator [package=78xxl]
  LED1 = LED - 5mm [color="Red (633nm)" package="5 mm [THT]"]
  R6 = Resistor [tolerance=±5% resistance=220 package=THT]
  D1 = Rectifier Diode [part_number=1N4001 package="300 mil [THT]"]
  Power_Switch = Toggle Switch [package=THT]
  D2 = Rectifier Diode [part_number=1N4001 package="300 mil [THT]"]
  D3 = Rectifier Diode [part_number=1N4001 package="300 mil [THT]"]
  I2C21 = female pin header, 4 pins [form="♀ (female)"]
  I2C11 = female pin header, 4 pins [form="♀ (female)"]
  I2C12 = female pin header, 4 pins [form="♀ (female)"]
  I2C22 = female pin header, 4 pins [form="♀ (female)"]
  D1_2 = female pin header, 2 pins [form="♀ (female)"]
  D2_2 = female pin header, 2 pins [form="♀ (female)"]
  D3_2 = female pin header, 2 pins [form="♀ (female)"]
  D4 = female pin header, 2 pins [form="♀ (female)"]
  D5 = female pin header, 2 pins [form="♀ (female)"]
  R7 = Resistor [tolerance=±5% resistance=10k package=THT]
  D6 = female pin header, 2 pins [form="♀ (female)"]
  R8 = Resistor [tolerance=±5% resistance=10k package=THT]
  D7 = female pin header, 2 pins [form="♀ (female)"]
  R9 = Resistor [tolerance=±5% resistance=10k package=THT]
  TTL1 = male pin header, 8 pins [form="♂ (male)"]
  LCH = male pin header, 4 pins [form="♂ (male)"]
  LCL = male pin header, 4 pins [form="♂ (male)"]
  TTL = male pin header, 3 pins [form="♂ (male)"]
  TTL2 = male pin header, 8 pins [form="♂ (male)"]  # not connected
  TTL3 = male pin header, 3 pins [form="♂ (male)"]
  BAT = screw terminal, 2 pins
  A03 = female pin header, 3 pins [form="♀ (female)"]
  A02 = female pin header, 3 pins [form="♀ (female)"]
  A01 = female pin header, 3 pins [form="♀ (female)"]
  SPI = female pin header, 9 pins [form="♀ (female)"]
  A04 = female pin header, 3 pins [form="♀ (female)"]
  A05 = female pin header, 3 pins [form="♀ (female)"]
  A06 = female pin header, 3 pins [form="♀ (female)"]
  A07 = female pin header, 3 pins [form="♀ (female)"]
  D0 = female pin header, 2 pins [form="♀ (female)"]
  R10 = Resistor [tolerance=±5% resistance=10k package=THT]
  D8 = female pin header, 2 pins [form="♀ (female)"]
  R11 = Resistor [tolerance=±5% resistance=10k package=THT]
  D9 = female pin header, 2 pins [form="♀ (female)"]
  R12 = Resistor [tolerance=±5% resistance=10k package=THT]
  D10 = female pin header, 2 pins [form="♀ (female)"]
  R13 = Resistor [tolerance=±5% resistance=10k package=THT]
  D11 = female pin header, 2 pins [form="♀ (female)"]
  R14 = Resistor [tolerance=±5% resistance=10k package=THT]
  D12 = female pin header, 2 pins [form="♀ (female)"]
  R15 = Resistor [tolerance=±5% resistance=10k package=THT]
  D13 = female pin header, 2 pins [form="♀ (female)"]
  R16 = Resistor [tolerance=±5% resistance=10k package=THT]
  D14 = female pin header, 2 pins [form="♀ (female)"]
  R17 = Resistor [tolerance=±5% resistance=10k package=THT]
  U5 = ATMEGA1284P [package=tqfn]
  R18 = Resistor [tolerance=±5% resistance=150k package=THT]
  R20 = Rotary Potentiometer (Small) [maximum_resistance=100kΩ package=THT]
  C6 = Tantalum Capacitor [capacitance=100µF voltage=16V package="200 mil [THT, tantalum]"]
  C5 = Tantalum Capacitor [capacitance=100nF voltage=16V package="200 mil [THT, tantalum]"]
  C8 = Ceramic Capacitor [capacitance=100nF package="100 mil [THT, multilayer]"]
  C9 = Ceramic Capacitor [capacitance=100nF package="100 mil [THT, multilayer]"]
  C10 = Ceramic Capacitor [capacitance=100nF package="100 mil [THT, multilayer]"]
  L1 = Inductor [package="400 mil [THT]"]
  C11 = Electrolytic Capacitor [capacitance=4.7µF package="100 mil [THT, electrolytic]"]
  XTAL1 = Crystal [frequency="16 Mhz" package=THT]
  C4 = Electrolytic Capacitor [capacitance=100nF voltage=16V package="200 mil [THT, electrolytic]"]

nets:
  GND: CT8z.pin1, R1.Pin_0, R2.Pin_0, R3.Pin_0, C1.0, C2.1, RESET.Pin_3, RESET.Pin_4, R5.Pin_0, U3.GND, U4.GND, LED1.cathode, I2C21.pin1, I2C11.pin1, I2C12.pin1, I2C22.pin1, R7.Pin_0, R8.Pin_0, R9.Pin_0, LCH.pin3, LCL.pin3, TTL.pin1, BAT.pin1, A03.pin1, A02.pin1, A01.pin1, SPI.pin2, SPI.pin8, A04.pin1, A05.pin1, A06.pin1, A07.pin1, R10.Pin_0, R11.Pin_0, R12.Pin_0, R13.Pin_0, R14.Pin_0, R15.Pin_0, R16.Pin_0, R17.Pin_0, U5.GND, R20.leg1, C6.-, C5.-, C8.1, C9.1, C10.0, C11.-, C4.-
  N1: CT8z.pin2, U4.IN, R6.Pin_1, D1.cathode, D3.cathode, R18.Pin_0, C6.+, C4.+
  N2: CT8z.pin3, U5.PD4*(OC1B)
  N3: R1.Pin_1, D2_2.pin1, U5.PD2(RX1)
  N4: R2.Pin_1, D1_2.pin1, U5.PD3(TX1)
  N5: R3.Pin_1, D3_2.pin1, A05.pin3, D10.pin1, R13.Pin_1, D14.pin1, R17.Pin_1, U5.PD6*(OC2B), U5.PC4, U5.PA2, U5.PB3*(OC0A)
  N6: C1.1, U5.XTAL1, XTAL1.pin_0
  N7: C2.0, U5.XTAL2, XTAL1.pin_1
  N8: R4.Pin_0, C3.1, RESET.Pin_1, RESET.Pin_2, SPI.pin9, U5.!RESET
  N9: R4.Pin_1, U3.IN, U4.OUT, D2.cathode, D3.anode, I2C11.pin2, I2C12.pin2, D1_2.pin2, D2_2.pin2, D3_2.pin2, D4.pin2, D5.pin2, D6.pin2, D7.pin2, LCH.pin4, TTL3.pin2, A03.pin2, A02.pin2, A01.pin2, SPI.pin1, A04.pin2, A05.pin2, A06.pin2, A07.pin2, D0.pin2, D8.pin2, D9.pin2, D10.pin2, D11.pin2, D12.pin2, D13.pin2, D14.pin2, U5.VCC, C5.+, C10.1, L1.pin_0, C11.+
  N10: C3.0, TTL1.pin1
  N11: R5.Pin_1, D4.pin1, U5.PB2
  N12: U3.OUT, D2.anode, I2C21.pin2, I2C22.pin2, LCL.pin4
  N13: LED1.anode, R6.Pin_0
  N14: D1.anode, Power_Switch.L2
  N15: Power_Switch.L1, Power_Switch.COM, BAT.pin2
  N16: I2C21.pin3, I2C22.pin3, LCL.pin2
  N17: I2C21.pin4, I2C22.pin4, LCL.pin1
  N18: I2C11.pin3, I2C12.pin3, LCH.pin2, U5.PC0(SDL)
  N19: I2C11.pin4, I2C12.pin4, LCH.pin1, U5.PC1(SDA)
  N20: D5.pin1, R7.Pin_1, U5.PB1
  N21: D6.pin1, R8.Pin_1, U5.PB0
  N22: D7.pin1, R9.Pin_1, U5.PC7
  N23: TTL.pin2, U5.PD1(TX0)
  N24: TTL.pin3, U5.PD0(RX0)
  N25: A03.pin3, U5.PA4
  N26: A02.pin3, U5.PA5
  N27: A01.pin3, U5.PA6
  N28: SPI.pin4, D9.pin1, R12.Pin_1, U5.PC5, U5.PB4*(SS_OC0B)
  N29: SPI.pin5, U5.PB5(MOSI)
  N30: SPI.pin6, U5.PB7*(SCK)
  N31: SPI.pin7, U5.PB6*(MISO)
  N32: A04.pin3, D0.pin1, R10.Pin_1, U5.PD5*(OC1A), U5.PA3
  N33: A06.pin3, U5.PA1
  N34: A07.pin3, U5.PA0
  N35: D8.pin1, R11.Pin_1, U5.PC6
  N36: D11.pin1, R14.Pin_1, U5.PC3
  N37: D12.pin1, R15.Pin_1, U5.PC2
  N38: D13.pin1, R16.Pin_1, U5.PD7*(OC2A)
  N39: U5.AVCC, C9.0, L1.pin_1
  N40: U5.AREF, C8.0
  N41: U5.PA7, R20.wiper
  N42: R18.Pin_1, R20.leg2

notes:
  V
  +
  TheSPT v2.0 R.R.
  D0: 13 A01: A0
  D1: 11 A02: A1
  D2: 10 A03: A2
  D3: 3 A04: A3
  D4: 2 A05: A4
  D5: 1 A06: A5
  D6: 0 A07: A6
  D7: 23
  D8: 22
  D9: 21
  D10: 20
  D11: 19
  D12: 18
  D13: 15
  D14: 14
  RADIO: 12
  BAT: A7

custom parts:
  ATMEGA1284P: Atmel 44-pin 8-bit Microcontroller with 128KBytes of ISP Flash and USB Controller

// code stored in the sketch: Transmiter.ino
#include <Wire.h>
#include <SPI.h>
#include <SD.h>

#include <LiquidCrystal_I2C.h>
#include <ADS1115.h>
#include <CT8Z.h>

#define DEBUG 1

#define POWER_MIN               10.0
#define POWER_MAX               11.56
#define POWER_RATIO1            (POWER_MAX / (3.85 * 1023 / 5))
#define POWER_RATIO2            (100.0 / (POWER_MAX - POWER_MIN))

#define BUTTON_NOT_PRESSED      0
#define BUTTON_PRESSED          (1 << 0)
#define BUTTON_LONG_PRESSED     (1 << 1)

#define STATE_IDLE              0
#define STATE_MODEL_MENU        1
#define STATE_SELECT_MODEL      2
#define STATE_CALIBRATE_MENU    3
#define STATE_CALIBRATE         4
#define STATE_CONFIGURE_MENU    5
#define STATE_SELECT_CHANNEL    6
#define STATE_CONFIGURE_SCALE   7
#define STATE_CONFIGURE_MIX     8
#define STATE_RESET_MENU        9
#define STATE_RESET             10
#define STATE_RETURN_IDLE       100

#define BUTTON_HOME             6
#define BUTTON_DOWN             2
#define BUTTON_UP               3

const char models[5][8] =
{
  "Model0",
  "Model1",
  "Model2",
  "Model3",
  "Model4"
};

class TransmiterChannel
{
friend class Transmiter;

public:
  int   scaleMin;
  int   scaleMax;
  int   mixChannel;
  float mixValue;
  
  void init(int axisValue, int trimValue, bool keepCalibration = false)
  {
    m_x = axisValue;
    if(!keepCalibration)
    {
      m_xMin = 0;
      m_xMax = 1023;
    }

    m_trimInit = trimValue;
    m_trimCurr = 0;
    
    scaleMin = 0;
    scaleMax = 1023;
    mixChannel = -1;
    mixValue = 0;
  }
  
  void beginCalibrate()
  {
    m_xMin = 512;
    m_xMax = 512;
  }

  void calibrate(int axisValue)
  {
    m_xMin = min(m_xMin, axisValue);
    m_xMax = max(m_xMax, axisValue);
  }

  void update(int axisValue, int trimValue)
  {
    if(trimValue > m_trimInit * 1.05)
    {
      m_trimCurr+=10;
    }
    else if(trimValue < m_trimInit * 0.95)
    {
      m_trimCurr-=10;
    } 
    m_x = map(axisValue, m_xMin, m_xMax, scaleMin, scaleMax) + m_trimCurr;
  }

  void readFromFile(File& file)
  {
    m_trimCurr = (file.read() << 8) + file.read();
    m_xMin = (file.read() << 8) + file.read();
    m_xMax = (file.read() << 8) + file.read();
    scaleMin = (file.read() << 8) + file.read();
    scaleMax = (file.read() << 8) + file.read();
    mixChannel = (file.read() << 8) + file.read();
    mixValue = ((file.read() << 8) + file.read()) / 100.0;
#ifdef DEBUG
    Serial.print(m_trimCurr);
    Serial.print("\t");
    Serial.print(m_xMin);
    Serial.print("\t");
    Serial.print(m_xMax);
    Serial.print("\t");
    Serial.print(scaleMin);
    Serial.print("\t");
    Serial.print(scaleMax);
    Serial.print("\t");
    Serial.print(mixChannel);
    Serial.print("\t");
    Serial.print(mixValue);
    Serial.println();
#endif
  }

  void writeToFile(File& file)
  {
#ifdef DEBUG
    Serial.print(m_trimCurr);
    Serial.print("\t");
    Serial.print(m_xMin);
    Serial.print("\t");
    Serial.print(m_xMax);
    Serial.print("\t");
    Serial.print(scaleMin);
    Serial.print("\t");
    Serial.print(scaleMax);
    Serial.print("\t");
    Serial.print(mixChannel);
    Serial.print("\t");
    Serial.print(mixValue);
    Serial.println();
#endif
    file.write(m_trimCurr >> 8); file.write(m_trimCurr);
    file.write(m_xMin >> 8); file.write(m_xMin);
    file.write(m_xMax >> 8); file.write(m_xMax);
    file.write(scaleMin >> 8); file.write(scaleMin);
    file.write(scaleMax >> 8); file.write(scaleMax);
    file.write(mixChannel >> 8); file.write(mixChannel);
    file.write((int)(mixValue * 100) >> 8); file.write((int)(mixValue * 100));
  }

private:
  int m_x;
  int m_xMin;
  int m_xMax;
  int m_trimCurr;
  int m_trimInit;
};

class Transmiter
{
public:
  TransmiterChannel channels[7];
  
  Transmiter():
    m_ads0(ADS1115_ADDRESS1),
    m_ads1(ADS1115_ADDRESS0)
  {
    
  }
  
  void init(File& file)
  {
    m_ads0.begin();
    m_ads1.begin();
    resetAll();
    loadAll(file);
    m_driver.begin();
  }

  void resetAll(bool keepCalibration = false)
  {
    channels[0].init(m_ads0.analogRead(ADS1115_A0) >> 4, m_ads0.analogRead(ADS1115_A2) >> 4, keepCalibration);
    channels[1].init(m_ads0.analogRead(ADS1115_A1) >> 4, m_ads0.analogRead(ADS1115_A3) >> 4, keepCalibration);
    channels[2].init(m_ads1.analogRead(ADS1115_A0) >> 4, m_ads1.analogRead(ADS1115_A2) >> 4, keepCalibration);
    channels[3].init(m_ads1.analogRead(ADS1115_A1) >> 4, m_ads1.analogRead(ADS1115_A3) >> 4, keepCalibration);
    channels[4].init(512, 0);
    channels[5].init(0, 0);
    channels[6].init(512, 0);
  }

  void loadAll(File& file)
  {
    if(file)
    {
      file.seek(0);
      for(int i = 0; i < 7; i++)
      {
        channels[i].readFromFile(file);
      }
      file.close();
    }
  }

  void saveAll(File& file)
  {
    if(file)
    {
      file.seek(0);
      for(int i = 0; i < 7; i++)
      {
        channels[i].writeToFile(file);
      }
      file.close();
    }
  }

  void beginCalibrate()
  {
    channels[0].beginCalibrate();
    channels[1].beginCalibrate();
    channels[2].beginCalibrate();
    channels[3].beginCalibrate();
  }

  void calibrate()
  {
    if(m_ads0.ready())
    {
      channels[0].calibrate(m_ads0.analogRead(ADS1115_A0) >> 4);
      channels[1].calibrate(m_ads0.analogRead(ADS1115_A1) >> 4);
    }
    if(m_ads1.ready())
    {
      channels[2].calibrate(m_ads1.analogRead(ADS1115_A0) >> 4);
      channels[3].calibrate(m_ads1.analogRead(ADS1115_A1) >> 4);
    }
  }

  void transmitAll()
  {
    if(m_ads0.ready())
    {
      channels[0].update(m_ads0.analogRead(ADS1115_A0) >> 4, m_ads0.analogRead(ADS1115_A2) >> 4);
      channels[1].update(m_ads0.analogRead(ADS1115_A1) >> 4, m_ads0.analogRead(ADS1115_A3) >> 4);
    }
    if(m_ads1.ready())
    {
      channels[2].update(m_ads1.analogRead(ADS1115_A0) >> 4, m_ads1.analogRead(ADS1115_A2) >> 4);
      channels[3].update(m_ads1.analogRead(ADS1115_A1) >> 4, m_ads1.analogRead(ADS1115_A3) >> 4);
    }
    channels[4].update(digitalRead(2) == HIGH ? 0 : (digitalRead(3) == HIGH  ? 1023 : 512), 0);
    channels[5].update(digitalRead(4) == HIGH  ? 1023 : 0, 0);
    channels[6].update(digitalRead(7) == HIGH  ? 0 : (digitalRead(8) == HIGH  ? 1023 : 512), 0);
    
    for(int i = 0; i < 7; i++)
    {
      TransmiterChannel* channel = &channels[i];
      if((channel->mixChannel == -1) || (channels[i].mixValue == 0))
      {
        m_driver.analogPulse(i, channel->m_x);
      }
      else if(channels[i].mixValue > 0)
      {
        m_driver.analogPulseMix(i, channels[channel->mixChannel].m_x, channel->m_x, channel->mixValue);
      }
      else
      {
        m_driver.analogPulseMix(i, 1023 - channels[channel->mixChannel].m_x, channel->m_x, -channel->mixValue);
      }
    }
  }

private:
  CT8Z      m_driver;
  ADS1115   m_ads0;
  ADS1115   m_ads1;
};

class Console
{
public:
  Console():
    m_lcd(0x27,16,2)
  {
  }

  void init()
  {
    m_lcd.init(); 
    m_lcd.backlight();
    m_lcd.print("Initializing ...");
    delay(1000);
  }

  void wakeup()
  {
    m_lcd.backlight();
  }
  
  void ready(const char* s)
  {
    delay(1000);
    m_lcd.noBacklight();
    m_lcd.clear();
    m_lcd.print(s);
    m_lcd.setCursor(0, 1);
    m_lcd.print("Ready");
  }

  void printTitle(const char* s)
  {
    m_lcd.clear();
    m_lcd.print(s);
  }

  void printCommand(const char* s)
  {
    m_lcd.setCursor(0, 1);
    m_lcd.print(s);
  }

  void printError(int error_code)
  {
    m_lcd.setCursor(0, 1);
    m_lcd.print("Error: 0x");
    m_lcd.print(error_code, HEX);
    delay(1000);
  }

  void printPercent(const int value)
  {
    m_lcd.setCursor(0, 1);
    m_lcd.print(value);
    m_lcd.print("%   ");
  }

  int pressButton(int pinNumber)
  {
    if(digitalRead(pinNumber) == HIGH)
    {
      int t = 0;
      while(digitalRead(pinNumber) == HIGH) { t++; delay(1); }
      return (t > 1000) ? BUTTON_LONG_PRESSED : BUTTON_PRESSED;
    }
    else
    {
      return BUTTON_NOT_PRESSED;
    }
  }
  
  void readValue(const char* label, int* value, int toLow, int toHigh)
  {
    while(pressButton(BUTTON_HOME) == LOW)
    {
      m_lcd.setCursor(0, 1);
      m_lcd.print(label);
      m_lcd.print(*value, DEC);
      m_lcd.print("    ");
      
      readIncDec(value, toLow, toHigh);
    }
  }

  void readPercent(const char* label, int* value, int toLow, int toHigh)
  {
    while(pressButton(BUTTON_HOME) == LOW)
    {
      m_lcd.setCursor(0, 1);
      m_lcd.print(label);
      m_lcd.print(*value, DEC);
      m_lcd.print("%   ");
      
      readIncDec(value, toLow, toHigh);
    }
  }

  void readYesNo(const char* label, int* value, int toLow, int toHigh)
  {
    while(pressButton(BUTTON_HOME) == LOW)
    {
      m_lcd.setCursor(0, 1);
      m_lcd.print(label);
      m_lcd.print(*value == 1 ? "Yes" : "No ");
      
      readIncDec(value, toLow, toHigh);
    }
  }

private:
  LiquidCrystal_I2C m_lcd;

  void readIncDec(int* value, int toLow, int toHigh)
  {
    if(digitalRead(BUTTON_UP) == HIGH)
    {
      while(digitalRead(BUTTON_UP) == HIGH) delay(1);
      *value = (*value >= toHigh) ? toLow : *value + 1;
    }
    if(digitalRead(BUTTON_DOWN) == HIGH)
    {
      while(digitalRead(BUTTON_DOWN) == HIGH) delay(1);
      *value = (*value <= toLow) ? toHigh : *value - 1;
    }
  
    delay(100);
  }
};

Console console;
Transmiter transmiter;

int state = STATE_IDLE;
int lastSelectedModel = 0;
int lastSelectedChannel = 0;

void idle()
{
  switch(console.pressButton(BUTTON_HOME))
  {
  case BUTTON_PRESSED:
    showPower();
    console.ready(models[lastSelectedModel]);
    break;
  case BUTTON_LONG_PRESSED:
    console.wakeup();
    state = STATE_MODEL_MENU;
    break;
  }
  transmiter.transmitAll();
}

void modelMenu()
{
  console.printTitle("Setup Menu"); 
  console.printCommand("Model"); 
  while(true)
  {
    switch(console.pressButton(BUTTON_HOME))
    {
    case BUTTON_PRESSED:
      state = STATE_SELECT_MODEL;
      return;
    case BUTTON_LONG_PRESSED:
      state = STATE_RETURN_IDLE;
      return;
    }
    if(console.pressButton(BUTTON_DOWN) == BUTTON_PRESSED)
    {
      state = STATE_RESET_MENU;
      return;
    }
    if(console.pressButton(BUTTON_UP) == BUTTON_PRESSED)
    {
      state = STATE_CALIBRATE_MENU;
      return;
    }
    delay(100);
  }
}

void selectModel()
{
  console.printTitle("Model");
  console.readValue("Select: ", &lastSelectedModel, 0, 4);

  File fileModel = SD.open(models[lastSelectedModel]);
  transmiter.loadAll(fileModel);
  
  state = STATE_MODEL_MENU;
}

void calibrateMenu()
{
  console.printTitle("Setup Menu"); 
  console.printCommand("Calibrate"); 
  while(true)
  {
    switch(console.pressButton(BUTTON_HOME))
    {
    case BUTTON_PRESSED:
      state = STATE_CALIBRATE;
      return;
    case BUTTON_LONG_PRESSED:
      state = STATE_RETURN_IDLE;
      return;
    }
    if(console.pressButton(BUTTON_DOWN) == BUTTON_PRESSED)
    {
      state = STATE_MODEL_MENU;
      return;
    }
    if(console.pressButton(BUTTON_UP) == BUTTON_PRESSED)
    {
      state = STATE_CONFIGURE_MENU;
      return;
    }
    delay(100);
  }
}

void calibrate()
{
  console.printTitle("Calibrate");
  
  console.printCommand("Center sticks");
  transmiter.beginCalibrate();
  while(console.pressButton(BUTTON_HOME) != BUTTON_PRESSED) delay(100);

  console.printCommand("Move sticks  ");
  while(console.pressButton(BUTTON_HOME) != BUTTON_PRESSED)
  {
    transmiter.calibrate();
  }

  state = STATE_CALIBRATE_MENU;
}

void configureMenu()
{
  console.printTitle("Setup Menu"); 
  console.printCommand("Configure");
  while(true)
  {
    switch(console.pressButton(BUTTON_HOME))
    {
    case BUTTON_PRESSED:
      state = STATE_SELECT_CHANNEL;
      return;
    case BUTTON_LONG_PRESSED:
      state = STATE_RETURN_IDLE;
      return;
    }
    if(console.pressButton(BUTTON_DOWN) == BUTTON_PRESSED)
    {
      state = STATE_CALIBRATE_MENU;
      return;
    }
    if(console.pressButton(BUTTON_UP) == BUTTON_PRESSED)
    {
      state = STATE_RESET_MENU;
      return;
    }
    delay(100);
  }
}

void selectChannel()
{
  console.printTitle("Configure");
  console.readValue("Select: ", &lastSelectedChannel, 0, 6);
  state = STATE_CONFIGURE_SCALE;
}

void configureScale()
{
  int v = 0;
  
  console.printTitle("Scale");
  v = (float(transmiter.channels[lastSelectedChannel].scaleMax - transmiter.channels[lastSelectedChannel].scaleMin) / 1023.0) * 100;
  console.readPercent("Value: ", &v, -100, 100);
  if(v >= 0)
  {
    transmiter.channels[lastSelectedChannel].scaleMin = 0;
    transmiter.channels[lastSelectedChannel].scaleMax = (float(v) / 100.0) * 1023;
  }
  else
  {
    transmiter.channels[lastSelectedChannel].scaleMin = 1023;
    transmiter.channels[lastSelectedChannel].scaleMax = (1.0 + float(v) / 100.0) * 1023;
  }
  //console.readValue("Min: ", &transmiter.channels[lastSelectedChannel].scaleMin, 0, 1023);
  //console.readValue("Max: ", &transmiter.channels[lastSelectedChannel].scaleMax, 0, 1023);
  state = STATE_CONFIGURE_MIX;
}

void configureMix()
{
  console.printTitle("Mix");
  console.readValue("Select: ", &transmiter.channels[lastSelectedChannel].mixChannel, 0, 6);
  if(transmiter.channels[lastSelectedChannel].mixChannel >= 0)
  {
    int v = transmiter.channels[lastSelectedChannel].mixValue * 100;
    console.readPercent("Value: ", &v, -100, 100);
    transmiter.channels[lastSelectedChannel].mixValue = v / 100.0;
  }
  state = STATE_CONFIGURE_MENU;
}

void resetMenu()
{
  console.printTitle("Setup Menu"); 
  console.printCommand("Reset");
  while(true)
  {
    switch(console.pressButton(BUTTON_HOME))
    {
    case BUTTON_PRESSED:
      state = STATE_RESET;
      return;
    case BUTTON_LONG_PRESSED:
      state = STATE_RETURN_IDLE;
      return;
    }
    if(console.pressButton(BUTTON_DOWN) == BUTTON_PRESSED)
    {
      state = STATE_CONFIGURE_MENU;
      return;
    }
    if(console.pressButton(BUTTON_UP) == BUTTON_PRESSED)
    {
      state = STATE_MODEL_MENU;
      return;
    }
    delay(100);
  }
}

void reset()
{
  int v = 0;
  
  console.printTitle("Reset");
  console.readYesNo("Sure? ", &v, 0, 1);
  if(v == 1)
  {
    transmiter.resetAll(true);
  }
  state = STATE_RESET_MENU;
}

void save()
{
  console.printTitle("Saving ...");
  
  File file = SD.open("conf", FILE_WRITE);
  if(!file)
  {
    console.printError(0x02);
    return;
  }
  file.seek(0);
  file.write(lastSelectedModel);
  file.close();
#ifdef DEBUG
    Serial.print(lastSelectedModel);
    Serial.println();
#endif
  
  file = SD.open(models[lastSelectedModel], FILE_WRITE);
  if (!file)
  {
    console.printError(0x03);
    return;
  }
  transmiter.saveAll(file);
  
  console.ready(models[lastSelectedModel]);
  state = STATE_IDLE;
}

void showPower()
{
  console.printTitle("Battery");
  console.printPercent(min(100, int((analogRead(A3) * POWER_RATIO1 - POWER_MIN) * POWER_RATIO2)));
}

void setup()
{
  console.init();
  
#ifdef DEBUG
  Serial.begin(19200);
#endif

  pinMode(2, INPUT);
  pinMode(3, INPUT);
  pinMode(4, INPUT);
  pinMode(6, INPUT);
  pinMode(7, INPUT);
  pinMode(8, INPUT);
  
  if(!SD.begin(9))
  {
    console.printError(0x01);
    return;
  }

  File file = SD.open("conf");
  if(file)
  {
    lastSelectedModel = file.read();
    file.close();
  }
#ifdef DEBUG
    Serial.print(lastSelectedModel);
    Serial.println();
#endif

  file = SD.open(models[lastSelectedModel]);
  transmiter.init(file);

  showPower();
  console.ready(models[lastSelectedModel]);
}

void loop()
{
  switch(state)
  {
  case STATE_IDLE:
    idle();
    break;
  case STATE_MODEL_MENU:
    modelMenu();
    break;
  case STATE_SELECT_MODEL:
    selectModel();
    break;
  case STATE_CALIBRATE_MENU:
    calibrateMenu();
    break;
  case STATE_CALIBRATE:
    calibrate();
    break;
  case STATE_CONFIGURE_MENU:
    configureMenu();
    break;
  case STATE_SELECT_CHANNEL:
    selectChannel();
    break;
  case STATE_CONFIGURE_SCALE:
    configureScale();
    break;
  case STATE_CONFIGURE_MIX:
    configureMix();
    break;
  case STATE_RESET_MENU:
    resetMenu();
    break;
  case STATE_RESET:
    reset();
    break;
  case STATE_RETURN_IDLE:
    save();
    break;
  }
}
