# Fritzing sketch WiiChuck (saved by Fritzing 0.9.3b)
circuit board: 3cm x 1.5cm
breadboards: 1

parts:
  Pad1 = Pad [width=10 height=1.5 connect=center]
  Pad3 = Pad [width=10 height=1.5 connect=center]
  Pad4 = Pad [width=5 height=1.5 connect=center]
  Pad5 = Pad [width=5 height=1.5 connect=center]
  Pad6 = Pad [width=5 height=1.5 connect=center]
  Pad7 = Pad [width=5 height=1.5 connect=center]
  Pad8 = Pad [width=10 height=1.5 connect=center]
  Pad9 = Pad [width=10 height=1.5 connect=center]
  Pad10 = Pad [width=5 height=1.5 connect=center]  # not connected
  Pad11 = Pad [width=5 height=1.5 connect=center]  # not connected
  Pad12 = Pad [width=5 height=1.5 connect=center]  # not connected
  Pad13 = Pad [width=5 height=1.5 connect=center]  # not connected
  Pad14 = Pad [width=5 height=1.5 connect=center]  # not connected

nets:
  N1: Pad1.pad, Pad5.pad
  N2: Pad3.pad, Pad7.pad
  N3: Pad4.pad, Pad9.pad
  N4: Pad6.pad, Pad8.pad
