# Fritzing sketch Accessories (saved by Fritzing 0.9.2b)
perfboards: 1

parts:
  S3 = Toggle Switch [package=THT]
  J2 = female pin header, 3 pins [form="♀ (female)"]
  J3 = female pin header, 3 pins [form="♀ (female)"]
  R3 = Resistor [tolerance=±5% resistance=1k package=THT]
  R4 = Resistor [tolerance=±5% resistance=1k package=THT]
  R7 = Resistor [tolerance=±5% resistance=1k package=THT]
  J4 = female pin header, 3 pins [form="♀ (female)"]
  S4 = Toggle Switch [package=THT]
  R8 = Resistor [tolerance=±5% resistance=1k package=THT]
  R9 = Resistor [tolerance=±5% resistance=1k package=THT]
  R10 = Resistor [tolerance=±5% resistance=1k package=THT]
  S5 = Pushbutton [package="[THT]"]
  S6 = Pushbutton [package="[THT]"]
  R11 = Resistor [tolerance=±5% resistance=1k package=THT]
  J5 = female pin header, 3 pins [form="♀ (female)"]

nets:
  N1: S3.L1, J2.pin3, R4.Pin_1
  N2: S3.COM, J2.pin2, J3.pin2
  N3: S3.L2, J3.pin3, R3.Pin_1
  N4: J2.pin1, R4.Pin_0
  N5: J3.pin1, R3.Pin_0
  N6: R7.Pin_0, J4.pin1
  N7: R7.Pin_1, J4.pin3, S4.L1
  N8: J4.pin2, S4.COM
  N9: R8.Pin_0, S5.Pin_3, S5.Pin_4, S6.Pin_3, S6.Pin_4, R11.Pin_1, J5.pin3
  N10: R8.Pin_1, R10.Pin_0, S5.Pin_1, S5.Pin_2
  GND: R9.Pin_0, J5.pin1
  N11: R9.Pin_1, S6.Pin_1, S6.Pin_2, R11.Pin_0
  5V: R10.Pin_1, J5.pin2
