# Fritzing sketch MainBoard (saved by Fritzing 0.9.2b)
circuit board: 18.5cm x 7.5cm

parts:
  CT8z = female pin header, 3 pins [form="♀ (female)"]
  R1 = Resistor [tolerance=±5% resistance=10k package=THT]
  R2 = Resistor [tolerance=±5% resistance=10k package=THT]
  R3 = Resistor [tolerance=±5% resistance=10k package=THT]
  U1 = atmega328 [package=dip]
  XTAL1 = Crystal [frequency="16 Mhz" package=THT]
  C1 = Ceramic Capacitor [capacitance=22pF package="100 mil [THT, multilayer]"]
  C2 = Ceramic Capacitor [capacitance=22pF package="100 mil [THT, multilayer]"]
  R4 = Resistor [tolerance=±5% resistance=10k package=THT]
  C3 = Ceramic Capacitor [capacitance=100nF package="100 mil [THT, multilayer]"]
  RESET = Pushbutton [package="[THT]"]
  R5 = Resistor [tolerance=±5% resistance=10k package=THT]
  C5 = Electrolytic Capacitor [capacitance=1µF voltage=16V package="100 mil [THT, electrolytic]"]
  U3 = V_REG_LD1117VXX [package=78xxl]
  U4 = Voltage Regulator [package=78xxl]
  LED1 = LED - 5mm [color="Red (633nm)" package="5 mm [THT]"]
  R6 = Resistor [tolerance=±5% resistance=220 package=THT]
  D1 = Rectifier Diode [part_number=1N4001 package="300 mil [THT]"]
  Power_Switch = Toggle Switch [package=THT]
  D2 = Rectifier Diode [part_number=1N4001 package="300 mil [THT]"]
  D3 = Rectifier Diode [part_number=1N4001 package="300 mil [THT]"]
  A23 = female pin header, 3 pins [form="♀ (female)"]
  A22 = female pin header, 3 pins [form="♀ (female)"]
  A21 = female pin header, 3 pins [form="♀ (female)"]
  A20 = female pin header, 3 pins [form="♀ (female)"]
  I2C21 = female pin header, 4 pins [form="♀ (female)"]
  I2C11 = female pin header, 4 pins [form="♀ (female)"]
  I2C12 = female pin header, 4 pins [form="♀ (female)"]
  C6 = Electrolytic Capacitor [capacitance=100µF voltage=16V package="100 mil [THT, electrolytic]"]
  I2C22 = female pin header, 4 pins [form="♀ (female)"]
  A13 = female pin header, 3 pins [form="♀ (female)"]
  A12 = female pin header, 3 pins [form="♀ (female)"]
  A10 = female pin header, 3 pins [form="♀ (female)"]
  A11 = female pin header, 3 pins [form="♀ (female)"]
  D1_2 = female pin header, 2 pins [form="♀ (female)"]
  D2_2 = female pin header, 2 pins [form="♀ (female)"]
  D3_2 = female pin header, 2 pins [form="♀ (female)"]
  D4 = female pin header, 2 pins [form="♀ (female)"]
  D5 = female pin header, 2 pins [form="♀ (female)"]
  R7 = Resistor [tolerance=±5% resistance=10k package=THT]
  D6 = female pin header, 2 pins [form="♀ (female)"]
  R8 = Resistor [tolerance=±5% resistance=10k package=THT]
  D7 = female pin header, 2 pins [form="♀ (female)"]
  R9 = Resistor [tolerance=±5% resistance=10k package=THT]
  TTL1 = male pin header, 8 pins [form="♂ (male)"]
  R10 = Resistor [tolerance=±5% resistance=10k package=THT]
  A03 = female pin header, 4 pins [form="♀ (female)"]
  LCH = male pin header, 4 pins [form="♂ (male)"]
  LCL = male pin header, 4 pins [form="♂ (male)"]
  A02 = female pin header, 4 pins [form="♀ (female)"]
  R11 = Resistor [tolerance=±5% resistance=10k package=THT]
  A01 = female pin header, 4 pins [form="♀ (female)"]
  R12 = Resistor [tolerance=±5% resistance=10k package=THT]
  R13 = Resistor [tolerance=±5% resistance=10k package=THT]
  A00 = female pin header, 4 pins [form="♀ (female)"]
  TTL = male pin header, 3 pins [form="♂ (male)"]
  TTL2 = male pin header, 8 pins [form="♂ (male)"]  # not connected
  TTL3 = male pin header, 3 pins [form="♂ (male)"]  # not connected
  C4 = Electrolytic Capacitor [capacitance=10µF voltage=16V package="200 mil [THT, electrolytic]"]
  ADS2 = male pin header, 10 pins [form="♂ (male)"]
  ADS1 = male pin header, 10 pins [form="♂ (male)"]
  BAT = screw terminal, 2 pins
  SPI = female pin header, 8 pins [form="♀ (female)"]

nets:
  GND: CT8z.pin1, R1.Pin_0, R2.Pin_0, R3.Pin_0, U1.GND, C1.0, C2.1, RESET.Pin_4, R5.Pin_0, C5.-, U3.GND, U4.GND, LED1.cathode, A23.pin1, A22.pin1, A21.pin1, A20.pin1, I2C11.pin2, I2C12.pin2, C6.-, A13.pin1, A12.pin1, A10.pin1, A11.pin1, R7.Pin_0, R8.Pin_0, R9.Pin_0, R10.Pin_0, A03.pin2, LCH.pin3, A02.pin2, R11.Pin_0, A01.pin2, R12.Pin_0, R13.Pin_0, A00.pin2, TTL.pin1, C4.-, ADS2.pin9, ADS1.pin5, ADS1.pin9, BAT.pin1, SPI.pin2
  N1: CT8z.pin2, U4.IN, R6.Pin_1, D1.cathode, D3.cathode, C6.+, C4.+
  N2: CT8z.pin3, U1.D10_(PWM)
  N3: R1.Pin_1, U1.D3_(PWM), D2_2.pin1
  N4: R2.Pin_1, U1.D2, D1_2.pin1
  N5: R3.Pin_1, U1.D4, D3_2.pin1
  N6: U1.RESET, R4.Pin_0, C3.1, RESET.Pin_1, RESET.Pin_2
  N7: U1.D0_(RX), TTL.pin3
  N8: U1.D1_(TX), TTL.pin2
  N9: U1.VCC, U1.AVCC, R4.Pin_1, C5.+, U3.IN, U4.OUT, D2.cathode, D3.anode, I2C11.pin1, I2C12.pin1, D1_2.pin2, D2_2.pin2, D3_2.pin2, D4.pin2, D5.pin2, D6.pin2, D7.pin2, A03.pin3, LCH.pin4, A02.pin3, A01.pin3, A00.pin3, SPI.pin1
  N10: U1.XLAT1, XTAL1.pin_1, C2.0
  N11: U1.XLAT2, XTAL1.pin_0, C1.1
  N12: U1.D5_(PWM), R5.Pin_1, D4.pin1
  N13: U1.D6_(PWM), D5.pin1, R7.Pin_1
  N14: U1.D7, D6.pin1, R8.Pin_1
  N15: U1.D8, D7.pin1, R9.Pin_1
  N16: U1.D9_(PWM), SPI.pin4
  N17: U1.D11_(PWM), SPI.pin5
  N18: U1.D12, SPI.pin7
  N19: U1.D13, SPI.pin6
  N20: U1.A0, A00.pin4
  N21: U1.A1, A01.pin4
  N22: U1.A2, A02.pin4
  N23: U1.A3, A03.pin4
  N24: U1.A4, I2C11.pin4, I2C12.pin4, LCH.pin1
  N25: U1.A5, I2C11.pin3, I2C12.pin3, LCH.pin2
  N26: C3.0, TTL1.pin1
  N27: U3.OUT, D2.anode, A23.pin2, A22.pin2, A21.pin2, A20.pin2, I2C21.pin1, I2C22.pin1, A13.pin2, A12.pin2, A10.pin2, A11.pin2, LCL.pin4, ADS2.pin5, ADS2.pin10, ADS1.pin10
  N28: LED1.anode, R6.Pin_0
  N29: D1.anode, Power_Switch.L2
  N30: Power_Switch.L1, Power_Switch.COM, BAT.pin2
  N31: A23.pin3, ADS1.pin1
  N32: A22.pin3, ADS1.pin2
  N33: A21.pin3, ADS1.pin3
  N34: A20.pin3, ADS1.pin4
  N35: I2C21.pin2, I2C22.pin2, LCL.pin3
  N36: I2C21.pin3, I2C22.pin3, LCL.pin2, ADS2.pin8, ADS1.pin8
  N37: I2C21.pin4, I2C22.pin4, LCL.pin1, ADS2.pin7, ADS1.pin7
  N38: A13.pin3, ADS2.pin1
  N39: A12.pin3, ADS2.pin2
  N40: A10.pin3, ADS2.pin4
  N41: A11.pin3, ADS2.pin3
  N42: R10.Pin_1, A03.pin1
  N43: A02.pin1, R11.Pin_1
  N44: A01.pin1, R12.Pin_1
  N45: R13.Pin_1, A00.pin1

// code stored in the sketch: Blink.ino
/*
  Blink
  Turns on an LED on for one second, then off for one second, repeatedly.

  Most Arduinos have an on-board LED you can control. On the Uno and
  Leonardo, it is attached to digital pin 13. If you're unsure what
  pin the on-board LED is connected to on your Arduino model, check
  the documentation at http://www.arduino.cc

  This example code is in the public domain.

  modified 8 May 2014
  by Scott Fitzgerald
 */


// the setup function runs once when you press reset or power the board
void setup() {
  // initialize digital pin 13 as an output.
  pinMode(3, OUTPUT);
}

// the loop function runs over and over again forever
void loop() {
  digitalWrite(3, HIGH);   // turn the LED on (HIGH is the voltage level)
  delay(1000);             // wait for a second
  digitalWrite(3, LOW);    // turn the LED off by making the voltage LOW
  delay(1000);              // wait for a second
}

// code stored in the sketch: Transmiter.ino
#include <Wire.h>
#include <wiinunchuck.h>
#include <ct8z.h>

WiiNunChuck nunc;
Ct8z transmitter;
int x, y;
int _k = LOW, k = LOW;
int s1 = LOW;

void setup()
{
	transmitter.begin();
	nunc.begin();
}

void loop()
{
  if(nunc.receive())
  {
    x = nunc.AX;
    y = nunc.AY;
  
    _k = k;
    k = nunc.BZ ? HIGH : LOW;
    if(_k == HIGH && k == LOW)
    {
      s1 = (s1 == LOW) ? HIGH : LOW;
    }
  }

  transmitter.analogWrite(0, x);
  transmitter.analogMix(1, y, 1023 - x, 0.8);
  transmitter.analogPulse(2, s1 == LOW ? 0 : 1023);
}
